// Logisim project CPU_JF_latest.circ as structural Verilog: 6 circuits, main circuit main
module main (
  input  Single_Step_Mode,
  input  Reset
);

  wire ALU_EN, and_2_out, and_3_out, and_4_out, CLK, CLK_out, cu_1_ici, cu_1_incpc, cu_1_reg_wr_en, DBG,
       decoder_1_out0, decoder_1_out1, decoder_1_out2, decoder_1_out3, decoder_1_out4, decoder_1_out5,
       decoder_1_out6, decoder_1_out7, Fl_WR_EN, LDC_EN, LDs12C_ALU, Mem_EN, Mem_WR_EN, MOV_R2PC, MOV_R2R,
       not_1_out, not_2_out, or_1_out, or_2_out, PC2ALU_A, Reg_A_EN, Release_DBG_out, s_r_ff_1_q, s_r_ff_1_qn;
  wire [2:0] cu_1_a, cu_1_b, cu_1_c, cu_1_result;
  wire [3:0] alu_1_flags, Flags;
  wire [4:0] cu_1_alu_cmd;
  wire [7:0] keyboard_1_data;
  wire [9:0] undriven;
  wire [14:0] cpu_register_1_portb;
  wire [15:0] alu_1_res, bit_extender_1_out, controlled_buffer_2_out, controlled_buffer_4_out,
       cpu_register_1_porta, cpu_register_1_portc, cu_1_ldc, PC_q, random_1_out, Result;
  wire [15:15] cpu_register_1_portb_2;
  wire [19:0] MEM_BUS_OUT;

  Comparator #(.width(20)) comparator_1 (.a(20'h7), .b(MEM_BUS_OUT), .eq(DBG));  // open: gt, lt
  Button Release_DBG (.out(Release_DBG_out));
  Clock u_CLK (.out(CLK_out));
  or or_1 (or_1_out, Single_Step_Mode, DBG);
  CU cu_1 (
    .PMemBus(MEM_BUS_OUT), .CLK(CLK), .Reset(Reset), .Flags(Flags), .incPC(cu_1_incpc),
    .ALU_CMD(cu_1_alu_cmd), .A(cu_1_a), .B(cu_1_b), .C(cu_1_c), .Reg_WR_EN(cu_1_reg_wr_en),
    .Result(cu_1_result), .LDC_EN(LDC_EN), .ALU_EN(ALU_EN), .MOV_R2R(MOV_R2R), .MOV_R2PC(MOV_R2PC),
    .LDs12C_ALU(LDs12C_ALU), .Reg_A_En(Reg_A_EN), .PC2ALU_A(PC2ALU_A), .Flag_WR_EN(Fl_WR_EN),
    .Mem_EN(Mem_EN), .Mem_WR_EN(Mem_WR_EN), .LDC(cu_1_ldc), .ICI(cu_1_ici));  // open: out_6, out_7, out_8, out_25
  S_R_Flip_Flop s_r_ff_1 (
    .S(or_1_out), .R(1'b0), .clk(CLK_out), .Q(s_r_ff_1_q), .reset(Release_DBG_out), .Qn(s_r_ff_1_qn));  // open: preset
  // NoConnect on s_r_ff_1_q
  not not_1 (not_1_out, cu_1_ici);
  and and_1 (CLK, cu_1_ici, CLK_out, s_r_ff_1_qn);
  LED ICnI (.in(not_1_out));
  Counter #(.max('hffff), .width(16)) PC (
    .load(MOV_R2PC), .D(Result), .count(cu_1_incpc), .Q(PC_q), .clk(CLK), .clr(Reset));  // open: carry, up
  assign bit_extender_1_out = {{4{cu_1_ldc[15]}}, cu_1_ldc[15:4]};  // Bit_Extender bit_extender_1
  ROM #(.addrWidth(16), .dataWidth(20)) PRG_MEM (.addr(PC_q), .data(MEM_BUS_OUT));
  assign Result = LDC_EN ? cu_1_ldc : 16'bz;  // Controlled_Buffer controlled_buffer_1
  assign controlled_buffer_2_out = LDs12C_ALU ? bit_extender_1_out : 16'bz;  // Controlled_Buffer controlled_buffer_2
  CPU_Register cpu_register_1 (
    .AddrC(cu_1_c), .Reset(Reset), .PortInp(Result), .AddrInp(cu_1_result), .CLK(CLK),
    .WR_EN(cu_1_reg_wr_en), .AddrA(cu_1_a), .AddrB(cu_1_b), .PortC(cpu_register_1_portc),
    .PortA(cpu_register_1_porta), .PortB({cpu_register_1_portb_2[15], cpu_register_1_portb}));
  assign Result = MOV_R2R ? cpu_register_1_porta : 16'bz;  // Controlled_Buffer controlled_buffer_3
  assign controlled_buffer_4_out = PC2ALU_A ? PC_q : 16'bz;  // Controlled_Buffer controlled_buffer_4
  assign controlled_buffer_4_out = Reg_A_EN ? cpu_register_1_porta : 16'bz;  // Controlled_Buffer controlled_buffer_5
  not not_2 (not_2_out, LDs12C_ALU);
  ALU alu_1 (
    .A(controlled_buffer_4_out), .CMD(cu_1_alu_cmd), .B(controlled_buffer_2_out), .C(cpu_register_1_portc),
    .FlagsInp(Flags), .Res(alu_1_res), .Flags(alu_1_flags));
  assign Result = ALU_EN ? alu_1_res : 16'bz;  // Controlled_Buffer controlled_buffer_6
  assign controlled_buffer_2_out = not_2_out ? {cpu_register_1_portb_2[15], cpu_register_1_portb} : 16'bz;  // Controlled_Buffer controlled_buffer_7
  Register #(.width(4)) Flag_Reg (.D(alu_1_flags), .en(Fl_WR_EN), .clk(CLK), .Q(Flags));  // open: clr
  and and_2 (and_2_out, Mem_WR_EN, ~cpu_register_1_portb_2[15]);  // AND_Gate
  and and_3 (and_3_out, ~cpu_register_1_portb_2[15], Mem_EN);  // AND_Gate
  or or_2 (or_2_out, Mem_WR_EN, Mem_EN);
  RAM #(.addrWidth(15), .dataWidth(16), .databus("bidir"), .\type ("nonvolatile")) ram_1 (
    .addr(cpu_register_1_portb), .we(and_2_out), .oe(and_3_out), .clk(CLK), .data(Result));
  and and_4 (and_4_out, or_2_out, cpu_register_1_portb_2[15]);
  Decoder #(.select(3)) decoder_1 (
    .out0(decoder_1_out0), .out1(decoder_1_out1), .out2(decoder_1_out2), .out3(decoder_1_out3),
    .out4(decoder_1_out4), .out5(decoder_1_out5), .out6(decoder_1_out6), .out7(decoder_1_out7),
    .sel(cpu_register_1_portb[2:0]), .en(and_4_out));
  TTY #(.rows(9)) tty_1 (.data(Result[6:0]), .clk(decoder_1_out0), .we(decoder_1_out0), .clr(decoder_1_out1));
  Keyboard #(.trigger("falling")) keyboard_1 (
    .clk(decoder_1_out2), .re(1'b1), .clr(decoder_1_out3), .avail(keyboard_1_data[7]),
    .data(keyboard_1_data[6:0]));
  assign Result[9:0] = decoder_1_out4 ? undriven : 10'bz;  // Controlled_Buffer controlled_buffer_8
  Joystick #(.bits(5)) joystick_1 ();  // open: x, y
  Random #(.width(16)) random_1 (.clr(decoder_1_out5), .next(decoder_1_out6), .clk(CLK), .out(random_1_out));
  assign Result = decoder_1_out2 ? {{8{1'b0}}, keyboard_1_data} : 16'bz;  // Controlled_Buffer controlled_buffer_9
  assign Result = decoder_1_out7 ? random_1_out : 16'bz;  // Controlled_Buffer controlled_buffer_10

  // Notes on the sheet:
  //   contents of PRG_MEM (hex, n*v repeats v):
  //   14080 a0 268 80080 29d 168 29d 168 29d 168 29d 168 29d 168 29d 168 29d 168 29d 168 29d 168 29d 168
  //   29d 168 29d 168 29d 168 29d 168 29d 168 29d 168 29d 168 29d 168 29d 168 29d 168 29d 168 14080 40069
  //   90 1108 2159 14080 40069 205 268 14082 90 168 b0 14082 40069 80080 79c 168 290 168 290 168 290 168
  //   290 168 205 14082 268 94 1108 159 fec58 90 80082 40069 1108 ffb59 80080 290 168 290 168 593 168 693
  //   168 69f 168 792 168 695 168 39a 168 290 168 290 168 9a 168 fc758 7f
  //   Text Buffer: Fallende Flanke -> fix early clearing
endmodule

module CPU_Register (
  input  CLK,
  input  [2:0] AddrA,
  input  [2:0] AddrB,
  input  [2:0] AddrC,
  input  Reset,
  input  [15:0] PortInp,
  input  [2:0] AddrInp,
  input  WR_EN,
  output [15:0] PortA,
  output [15:0] PortB,
  output [15:0] PortC
);

  wire decoder_1_out0, decoder_1_out1, decoder_1_out2, decoder_1_out3, decoder_1_out4, decoder_1_out5,
       decoder_1_out6, decoder_1_out7;
  wire [15:0] register_1_q, register_2_q, register_3_q, register_4_q, register_5_q, register_6_q,
       register_7_q, register_8_q;

  Decoder #(.select(3)) decoder_1 (
    .out0(decoder_1_out0), .out1(decoder_1_out1), .out2(decoder_1_out2), .out3(decoder_1_out3),
    .out4(decoder_1_out4), .out5(decoder_1_out5), .out6(decoder_1_out6), .out7(decoder_1_out7),
    .sel(AddrInp), .en(WR_EN));
  Register #(.width(16)) register_1 (.D(PortInp), .en(decoder_1_out0), .clk(CLK), .Q(register_1_q), .clr(Reset));
  Register #(.width(16)) register_2 (.D(PortInp), .en(decoder_1_out1), .clk(CLK), .Q(register_2_q), .clr(Reset));
  Register #(.width(16)) register_3 (.D(PortInp), .en(decoder_1_out2), .clk(CLK), .Q(register_3_q), .clr(Reset));
  Register #(.width(16)) register_4 (.D(PortInp), .en(decoder_1_out3), .clk(CLK), .Q(register_4_q), .clr(Reset));
  Register #(.width(16)) register_5 (.D(PortInp), .en(decoder_1_out4), .clk(CLK), .Q(register_5_q), .clr(Reset));
  Register #(.width(16)) register_6 (.D(PortInp), .en(decoder_1_out5), .clk(CLK), .Q(register_6_q), .clr(Reset));
  Register #(.width(16)) register_7 (.D(PortInp), .en(decoder_1_out6), .clk(CLK), .Q(register_7_q), .clr(Reset));
  Register #(.width(16)) register_8 (.D(PortInp), .en(decoder_1_out7), .clk(CLK), .Q(register_8_q), .clr(Reset));
  Multiplexer #(.select(3), .width(16)) multiplexer_1 (
    .in0(register_1_q), .in1(register_2_q), .in2(register_3_q), .in3(register_4_q), .in4(register_5_q),
    .in5(register_6_q), .in6(register_7_q), .in7(register_8_q), .out(PortA), .sel(AddrA));
  Multiplexer #(.select(3), .width(16)) multiplexer_2 (
    .in0(register_1_q), .in1(register_2_q), .in2(register_3_q), .in3(register_4_q), .in4(register_5_q),
    .in5(register_6_q), .in6(register_7_q), .in7(register_8_q), .out(PortB), .sel(AddrB));
  Multiplexer #(.select(3), .width(16)) multiplexer_3 (
    .in0(register_1_q), .in1(register_2_q), .in2(register_3_q), .in3(register_4_q), .in4(register_5_q),
    .in5(register_6_q), .in6(register_7_q), .in7(register_8_q), .out(PortC), .sel(AddrC));
endmodule

module CU (
  input  [19:0] PMemBus,
  input  CLK,
  input  Reset,
  input  [3:0] Flags,
  output incPC,
  output out_6,
  output out_7,
  output out_8,
  output [4:0] ALU_CMD,
  output [2:0] A,
  output [2:0] B,
  output [2:0] C,
  output Reg_WR_EN,
  output [2:0] Result,
  output LDC_EN,
  output ALU_EN,
  output MOV_R2R,
  output MOV_R2PC,
  output LDs12C_ALU,
  output Reg_A_En,
  output PC2ALU_A,
  output Flag_WR_EN,
  output Mem_EN,
  output Mem_WR_EN,
  output out_25,
  output [15:0] LDC,
  output ICI
);

  wire comparator_1_eq, DecodeIW, FetchIW, Flag_Mux_q, ldc_select_1_ldc_active, multiplexer_3_out, not_1_out,
       or_1_out;
  wire [1:0] CPU_Status_q;
  wire [2:0] Flag_select, InstructionWord_q, multiplexer_1_out;
  wire [7:0] ldc_select_1_iw_const, multiplexer_4_out;
  wire [7:7] InstructionWord_q_2;

  Register #(.width(20)) InstructionWord (
    .D(PMemBus), .en(FetchIW), .clk(CLK),
    .Q({LDC[15:13], C, B, A, InstructionWord_q_2[7], InstructionWord_q, LDC[3:0]}), .clr(Reset));
  Counter #(.max('h3), .width(2)) CPU_Status (
    .Q(CPU_Status_q), .clk(CLK), .clr(Reset));  // open: load, D, count, carry, up
  Comparator comparator_1 (
    .a(8'h5), .b({InstructionWord_q_2[7], InstructionWord_q, LDC[3:0]}), .eq(comparator_1_eq));  // open: gt, lt
  Multiplexer #(.width(3)) multiplexer_1 (
    .in0(LDC[15:13]), .in1(InstructionWord_q), .out(multiplexer_1_out), .sel(ldc_select_1_ldc_active));
  not not_1 (not_1_out, comparator_1_eq);
  LDC_select ldc_select_1 (
    .IW({InstructionWord_q_2[7], InstructionWord_q, LDC[3:0]}), .IW_const(ldc_select_1_iw_const),
    .LDC_active(ldc_select_1_ldc_active));
  Multiplexer #(.width(3)) multiplexer_2 (.in0(A), .in1(multiplexer_1_out), .out(Result), .sel(not_1_out));
  Multiplexer #(.select(2)) multiplexer_3 (
    .in0(Flags[0]), .in1(Flags[1]), .in2(Flags[2]), .in3(Flags[3]), .out(multiplexer_3_out),
    .sel(Flag_select[1:0]));
  or or_1 (or_1_out, multiplexer_3_out, ~Flag_select[2]);  // OR_Gate
  Multiplexer #(.width(8)) multiplexer_4 (
    .in0(8'h6c), .in1(ldc_select_1_iw_const), .out(multiplexer_4_out), .sel(Flag_Mux_q));
  Register #(.width(1)) Flag_Mux (.D(or_1_out), .en(DecodeIW), .clk(CLK), .Q(Flag_Mux_q));  // open: clr
  ROM #(.addrWidth(10), .dataWidth(16)) MicroProgramMem (
    .addr({multiplexer_4_out, CPU_Status_q}),
    .data({out_25, Mem_WR_EN, Mem_EN, Flag_WR_EN, PC2ALU_A, Reg_A_En, LDs12C_ALU, MOV_R2PC, MOV_R2R, ALU_EN, LDC_EN, Reg_WR_EN, Flag_select, ICI}));
  and and_1 (DecodeIW, CPU_Status_q[0], ~CPU_Status_q[1]);  // AND_Gate
  and and_2 (FetchIW, ~CPU_Status_q[1], ~CPU_Status_q[0]);  // AND_Gate
  and and_3 (incPC, CPU_Status_q[0], ~CPU_Status_q[1]);  // AND_Gate
  Multiplexer #(.width(5)) multiplexer_5 (
    .in0(multiplexer_4_out[4:0]), .in1({5{1'b0}}), .out(ALU_CMD), .sel(LDs12C_ALU));

  assign LDC[12:4] = {C, B, A};

  // Notes on the sheet:
  //   Instruction Word
  //   17 .. 19 Result
  //   0 - Carry
  //   1 - Overflow
  //   2 - Zero
  //   3 - not Zero
  //   contents of MicroProgramMem (hex, n*v repeats v):
  //   1 1 1441 1451 1 1 1441 1451 1 1 441 1451 1 1 1441 1451 1 1 441 1451 1 1 1441 1451 1 1 1441 1451 1 1
  //   1441 1451 1 1 1441 1441 1 1 1441 1451 1 1 1441 1451 1 1 1441 1451 1 1 1441 1451 1 1 1441 1451 1 1
  //   1441 1451 1 1 1441 1451 1 1 1441 1451 188*0 1 1 81 181 28*0 1 81 81 91 28*0 d 81 81 181 d 8d 8d 18d
  //   f 8f 8f 18f 9 89 89 189 16*0 d a01 a41 b41 d a0d a4d b4d f a0f a4f b4f 9 a09 a49 b49 16*0 4*1 28*0 1
  //   1 4481 4481 1 1 2011 2011 8*0 4*1 68*0 4*1 4*0 1 1 31 31
  //   LDs12C_ALU
  //   LSB 4 Bit Inner
  //   +0010
  //   +0020
  //   +0040
  //   +0080
  //   +0100
  //   +0200
  //   +0400
  //   +0800
  //   +1000
  //   +2000
  //   +4000
  //   Instruction Code implemented
  //   Register Write Enable
  //   Load Constant
  //   ALU Enable
  //   Move Register to Register
  //   CPU Register Port A Enable
  //   Program Counter to ALU A
  //   Flag Write Enable
  //   Memory Enable
  //   Memory Write Enable
  //   Move Register to Program Counter
  //   Load signed 12 bit constant into ALU
endmodule

module ALU (
  input  [15:0] A,
  input  [15:0] B,
  input  [15:0] C,
  input  [3:0] FlagsInp,
  input  [4:0] CMD,
  output [3:0] Flags,
  output [15:0] Res
);

  wire adder_1_cout, adder_2_cout, adder_3_cout, adder_4_cout, adder_5_cout, or_2_out, or_3_out, or_4_out,
       overflow_detect_1_overflow, overflow_detect_2_overflow, overflow_detect_3_overflow,
       overflow_detect_4_overflow, overflow_detect_5_overflow, overflow_detect_6_overflow,
       overflow_detect_7_overflow, overflow_detect_8_overflow, overflow_detect_9_overflow,
       overflow_detect_10_overflow, overflow_detect_11_overflow, SignFlag, subtractor_1_bout,
       subtractor_2_bout, subtractor_3_bout, subtractor_4_bout;
  wire [15:0] adder_1_out, adder_2_out, adder_3_out, adder_4_out, adder_5_out, adder_6_out, and_1_out,
       multiplier_1_cout, multiplier_1_out, negator_1_out, not_1_out, not_2_out, not_3_out, not_4_out,
       or_1_out, shifter_1_out, shifter_2_out, subtractor_1_out, subtractor_2_out, subtractor_3_out,
       subtractor_4_out, undriven, undriven_2, undriven_3, undriven_4, undriven_5, undriven_6, undriven_7,
       undriven_8, undriven_9, undriven_10, undriven_11, undriven_12, undriven_13, undriven_14, undriven_15,
       xnor_1_out, xor_1_out;

  Adder #(.width(16)) adder_1 (.a(A), .b(B), .out(adder_1_out), .cout(adder_1_cout));  // open: cin
  Overflow_detect overflow_detect_1 (.A(A), .B(B), .Y(adder_1_out), .Overflow(overflow_detect_1_overflow));
  Adder #(.width(16)) adder_2 (.a(A), .b(B), .out(adder_2_out), .cout(adder_2_cout));  // open: cin
  Overflow_detect overflow_detect_2 (.A(A), .B(B), .Y(adder_2_out), .Overflow(overflow_detect_2_overflow));
  Adder #(.width(16)) adder_3 (.a(A), .b(B), .out(adder_3_out), .cin(FlagsInp[0]), .cout(adder_3_cout));
  Overflow_detect overflow_detect_3 (.A(A), .B(B), .Y(adder_3_out), .Overflow(overflow_detect_3_overflow));
  Subtractor #(.width(16)) subtractor_1 (.a(A), .b(B), .out(subtractor_1_out), .bout(subtractor_1_bout));  // open: bin
  Overflow_detect overflow_detect_4 (.A(A), .B(not_1_out), .Y(subtractor_1_out), .Overflow(overflow_detect_4_overflow));
  assign not_1_out = ~B;  // NOT_Gate not_1, 16 bits wide
  Subtractor #(.width(16)) subtractor_2 (
    .a(A), .b(B), .out(subtractor_2_out), .bin(FlagsInp[0]), .bout(subtractor_2_bout));
  Overflow_detect overflow_detect_5 (.A(A), .B(not_2_out), .Y(subtractor_2_out), .Overflow(overflow_detect_5_overflow));
  assign not_2_out = ~B;  // NOT_Gate not_2, 16 bits wide
  Adder #(.width(16)) adder_4 (.a(A), .b(16'h1), .out(adder_4_out), .cout(adder_4_cout));  // open: cin
  Overflow_detect overflow_detect_6 (.A(A), .B(16'h1), .Y(adder_4_out), .Overflow(overflow_detect_6_overflow));
  Subtractor #(.width(16)) subtractor_3 (
    .a(A), .b(16'h1), .out(subtractor_3_out), .bout(subtractor_3_bout));  // open: bin
  Overflow_detect overflow_detect_7 (.A(A), .B(not_3_out), .Y(subtractor_3_out), .Overflow(overflow_detect_7_overflow));
  assign not_3_out = ~16'h1;  // NOT_Gate not_3, 16 bits wide
  Multiplier #(.width(16)) multiplier_1 (.a(A), .b(B), .out(multiplier_1_out), .cout(multiplier_1_cout));  // open: cin
  Overflow_detect overflow_detect_8 (.A(A), .B(B), .Y(multiplier_1_out), .Overflow(overflow_detect_8_overflow));
  Subtractor #(.width(16)) subtractor_4 (.a(A), .b(B), .out(subtractor_4_out), .bout(subtractor_4_bout));  // open: bin
  Overflow_detect overflow_detect_9 (.A(A), .B(B), .Y(subtractor_4_out), .Overflow(overflow_detect_9_overflow));
  assign and_1_out = A & B;  // AND_Gate and_1, 16 bits wide
  assign or_1_out = A | B;  // OR_Gate or_1, 16 bits wide
  assign not_4_out = ~A;  // NOT_Gate not_4, 16 bits wide
  Negator #(.width(16)) negator_1 (.in(A), .out(negator_1_out));
  assign xor_1_out = A ^ B;  // XOR_Gate xor_1, 16 bits wide
  assign xnor_1_out = ~(A ^ B);  // XNOR_Gate xnor_1, 16 bits wide
  Shifter #(.width(16)) shifter_1 (.in(A), .\dist (B[3:0]), .out(shifter_1_out));
  Shifter #(.shift("lr"), .width(16)) shifter_2 (.in(A), .\dist (B[3:0]), .out(shifter_2_out));
  Adder #(.width(16)) adder_5 (.a(adder_2_out), .b(C), .out(adder_5_out), .cin(adder_2_cout), .cout(adder_5_cout));
  Overflow_detect overflow_detect_10 (.A(adder_2_out), .B(C), .Y(adder_5_out), .Overflow(overflow_detect_10_overflow));
  or or_2 (or_2_out, overflow_detect_10_overflow, overflow_detect_2_overflow);
  or or_3 (or_3_out, multiplier_1_cout[0], multiplier_1_cout[1], multiplier_1_cout[2], multiplier_1_cout[3], multiplier_1_cout[4], multiplier_1_cout[5], multiplier_1_cout[6], multiplier_1_cout[7]);
  or or_4 (or_4_out, multiplier_1_cout[8], multiplier_1_cout[9], multiplier_1_cout[10], multiplier_1_cout[11], multiplier_1_cout[12], multiplier_1_cout[13], multiplier_1_cout[14], multiplier_1_cout[15], or_3_out);
  Multiplexer #(.select(5), .width(16)) multiplexer_1 (
    .in0(adder_1_out), .in1(adder_5_out), .in2(adder_3_out), .in3(subtractor_1_out), .in4(subtractor_2_out),
    .in5(adder_4_out), .in6(subtractor_3_out), .in7(multiplier_1_out), .in8(subtractor_4_out),
    .in9(and_1_out), .in10(or_1_out), .in11(not_4_out), .in12(negator_1_out), .in13(xor_1_out),
    .in14(xnor_1_out), .in15(shifter_1_out), .in16(shifter_2_out), .in17(undriven), .in18(undriven_2),
    .in19(undriven_3), .in20(undriven_4), .in21(undriven_5), .in22(undriven_6), .in23(undriven_7),
    .in24(undriven_8), .in25(undriven_9), .in26(undriven_10), .in27(undriven_11), .in28(undriven_12),
    .in29(undriven_13), .in30(undriven_14), .in31(undriven_15), .out(Res), .sel(CMD));
  Multiplexer #(.select(5)) multiplexer_2 (
    .in0(adder_1_cout), .in1(adder_5_cout), .in2(adder_3_cout), .in3(subtractor_1_bout),
    .in4(subtractor_2_bout), .in5(adder_4_cout), .in6(subtractor_3_bout), .in7(or_4_out),
    .in8(subtractor_4_bout), .in9(1'b0), .in10(1'b0), .in11(1'b0), .in12(1'b0), .in13(1'b0), .in14(1'b0),
    .in15(1'b0), .in16(1'b0), .out(Flags[0]), .sel(CMD));  // open: in17, in18, in19, in20, in21, in22, in23, in24, in25, in26, in27, in28, in29, in30, in31
  Multiplexer #(.select(5)) multiplexer_3 (
    .in0(overflow_detect_1_overflow), .in1(or_2_out), .in2(overflow_detect_3_overflow),
    .in3(overflow_detect_4_overflow), .in4(overflow_detect_5_overflow), .in5(overflow_detect_6_overflow),
    .in6(overflow_detect_7_overflow), .in7(overflow_detect_8_overflow), .in8(overflow_detect_9_overflow),
    .in9(1'b0), .in10(1'b0), .in11(1'b0), .in12(1'b0), .in13(1'b0), .in14(1'b0), .in15(1'b0), .in16(1'b0),
    .out(Flags[1]), .sel(CMD));  // open: in17, in18, in19, in20, in21, in22, in23, in24, in25, in26, in27, in28, in29, in30, in31
  Multiplexer #(.select(5)) multiplexer_4 (
    .in0(adder_1_out[15]), .in1(adder_5_out[15]), .in2(adder_3_out[15]), .in3(subtractor_1_out[15]),
    .in4(subtractor_2_out[15]), .in5(adder_4_out[15]), .in6(subtractor_3_out[15]),
    .in7(multiplier_1_out[15]), .in8(subtractor_4_out[15]), .in9(1'b0), .in10(1'b0), .in11(1'b0),
    .in12(1'b0), .in13(1'b0), .in14(1'b0), .in15(1'b0), .in16(1'b0), .out(SignFlag), .sel(CMD));  // open: in17, in18, in19, in20, in21, in22, in23, in24, in25, in26, in27, in28, in29, in30, in31
  nor nor_1 (Flags[2], Res[0], Res[1], Res[2], Res[3], Res[4], Res[5], Res[6], Res[7], Res[8], Res[9], Res[10], Res[11], Res[12], Res[13], Res[14], Res[15]);
  Adder #(.width(16)) adder_6 (.a(16'h7fff), .b(16'h1), .out(adder_6_out));  // open: cin, cout
  Overflow_detect overflow_detect_11 (.A(16'h7fff), .B(16'h1), .Y(adder_6_out), .Overflow(overflow_detect_11_overflow));
  not not_5 (Flags[3], Flags[2]);

  // Other names for the same wires on the sheet: CarryFlag = Flags[0]; OverflowFlag = Flags[1]; ZeroFlag = Flags[2]

  // Notes on the sheet:
  //   0
  //   1
  //   2
  //   3
  //   4
  //   5
  //   6
  //   7
  //   8
  //   9
  //   10
  //   11
  //   12
  //   13
  //   14
  //   15
  //   16
  //   Flags: 0 - Carry
  //   1 - Overflow
  //   2 - Zero
  //   3 - Sign
  //   ADD2
  //   ADD3
  //   ADC
  //   SUB
  //   SUBC
  //   INC
  //   DEC
  //   MUL
  //   TST
  //   AND
  //   OR
  //   NOT
  //   NEG
  //   XOR
  //   XNOR
  //   SHL
  //   SHR
  //   Sign
  //   Overflow
  //   Carry
  //   NotZeroFlag
endmodule

module LDC_select (
  input  [7:0] IW,
  output [7:0] IW_const,
  output LDC_active
);

  wire not_1_out;

  assign IW_const[6:0] = IW[7] ? {7{1'b0}} : 7'bz;  // Controlled_Buffer controlled_buffer_1
  not not_1 (not_1_out, IW[7]);
  assign IW_const[6:0] = not_1_out ? IW[6:0] : 7'bz;  // Controlled_Buffer controlled_buffer_2

  assign IW_const[7] = IW[7];
  assign LDC_active = IW[7];
endmodule

module Overflow_detect (
  input  [15:0] A,
  input  [15:0] B,
  input  [15:0] Y,
  output Overflow
);

  wire and_1_out, and_2_out, bitselector_1_out, bitselector_2_out, bitselector_3_out;

  BitSelector #(.width(16)) bitselector_1 (.in(A), .out(bitselector_1_out), .sel(4'b1111));
  BitSelector #(.width(16)) bitselector_2 (.in(B), .out(bitselector_2_out), .sel(4'b1111));
  BitSelector #(.width(16)) bitselector_3 (.in(Y), .out(bitselector_3_out), .sel(4'b1111));
  and and_1 (and_1_out, bitselector_1_out, bitselector_2_out, ~bitselector_3_out);  // AND_Gate
  and and_2 (and_2_out, ~bitselector_1_out, ~bitselector_2_out, bitselector_3_out);  // AND_Gate
  or or_1 (Overflow, and_1_out, and_2_out);
endmodule
